// Logisim project Full_Clock.circ as structural Verilog: 5 circuits, main circuit UI
module Contador_0_9 (
  input  a0,
  input  a1,
  input  a2,
  input  a3,
  output a0p,
  output a1p,
  output a2p,
  output a3p
);

  wire and_1_out, and_2_out, and_3_out, and_4_out, and_5_out, and_6_out, and_7_out, not_1_out, not_2_out,
       not_3_out, not_4_out, not_5_out, not_6_out, not_7_out;

  and and_1 (and_1_out, a1, a2, a3);
  and and_2 (and_2_out, a0, not_1_out);
  not not_1 (not_1_out, a3);
  not not_2 (not_2_out, a1);
  and and_3 (and_3_out, not_2_out, a2, a3);
  and and_4 (and_4_out, a1, not_3_out);
  not not_3 (not_3_out, a2);
  and and_5 (and_5_out, a1, not_4_out);
  not not_4 (not_4_out, a3);
  not not_5 (not_5_out, a0);
  not not_6 (not_6_out, a2);
  and and_6 (and_6_out, not_5_out, not_6_out, a3);
  and and_7 (and_7_out, a2, not_7_out);
  not not_7 (not_7_out, a3);
  not not_8 (a3p, a3);
  or or_1 (a0p, and_1_out, and_2_out);
  or or_2 (a1p, and_3_out, and_4_out, and_5_out);
  or or_3 (a2p, and_6_out, and_7_out);
endmodule

module Contador_0_5 (
  input  a0,
  input  a1,
  input  a2,
  output a0p,
  output a1p,
  output a2p
);

  wire and_1_out, and_2_out, and_3_out, and_4_out, not_1_out, not_2_out, not_3_out, not_4_out;

  not not_1 (not_1_out, a2);
  not not_2 (not_2_out, a0);
  not not_3 (not_3_out, a1);
  not not_4 (not_4_out, a2);
  not not_5 (a2p, a2);
  and and_1 (and_1_out, a1, a2);
  and and_2 (and_2_out, a0, not_1_out);
  and and_3 (and_3_out, not_2_out, not_3_out, a2);
  and and_4 (and_4_out, a1, not_4_out);
  or or_1 (a0p, and_1_out, and_2_out);
  or or_2 (a1p, and_3_out, and_4_out);
endmodule

module Flip_0_9 (
  input  clk,
  output [3:0] out_2,
  output clk_out
);

  wire contador_0_9_1_a0p, contador_0_9_1_a1p, contador_0_9_1_a2p, contador_0_9_1_a3p;

  D_Flip_Flop d_ff_1 (.clk(clk), .D(contador_0_9_1_a0p), .Q(out_2[3]));  // open: Qn, preset, en, reset
  D_Flip_Flop d_ff_2 (.clk(clk), .D(contador_0_9_1_a1p), .Q(out_2[2]));  // open: Qn, preset, en, reset
  Contador_0_9 contador_0_9_1 (
    .a0(out_2[3]), .a1(out_2[2]), .a2(out_2[1]), .a3(out_2[0]), .a0p(contador_0_9_1_a0p),
    .a1p(contador_0_9_1_a1p), .a2p(contador_0_9_1_a2p), .a3p(contador_0_9_1_a3p));
  D_Flip_Flop d_ff_3 (.clk(clk), .D(contador_0_9_1_a2p), .Q(out_2[1]));  // open: Qn, preset, en, reset
  D_Flip_Flop d_ff_4 (.clk(clk), .D(contador_0_9_1_a3p), .Q(out_2[0]));  // open: Qn, preset, en, reset
  nor nor_1 (clk_out, out_2[0], out_2[1], out_2[2], out_2[3]);
endmodule

module Flip_0_5 (
  input  clk,
  output [2:0] out_2,
  output clk_out
);

  wire contador_0_5_1_a0p, contador_0_5_1_a1p, contador_0_5_1_a2p;

  D_Flip_Flop d_ff_1 (.clk(clk), .D(contador_0_5_1_a0p), .Q(out_2[2]));  // open: Qn, preset, en, reset
  Contador_0_5 contador_0_5_1 (
    .a0(out_2[2]), .a1(out_2[1]), .a2(out_2[0]), .a0p(contador_0_5_1_a0p), .a1p(contador_0_5_1_a1p),
    .a2p(contador_0_5_1_a2p));
  D_Flip_Flop d_ff_2 (.clk(clk), .D(contador_0_5_1_a1p), .Q(out_2[1]));  // open: Qn, preset, en, reset
  D_Flip_Flop d_ff_3 (.clk(clk), .D(contador_0_5_1_a2p), .Q(out_2[0]));  // open: Qn, preset, en, reset
  nor nor_1 (clk_out, out_2[0], out_2[1], out_2[2]);
endmodule

module UI (
);

  wire clock_1_out, flip_0_5_2_clk_out, flip_0_9_1_clk_out, flip_0_9_2_clk_out;
  wire [2:0] flip_0_5_1_out_2, flip_0_5_2_out_2;
  wire [3:0] flip_0_9_1_out_2, flip_0_9_2_out_2;

  Flip_0_5 flip_0_5_1 (.clk(flip_0_9_1_clk_out), .out_2(flip_0_5_1_out_2));  // open: clk_out
  Hex_Digit_Display hex_digit_display_1 (.value({1'b0, flip_0_5_1_out_2}), .dp(1'b0));
  Flip_0_9 flip_0_9_1 (.clk(flip_0_5_2_clk_out), .out_2(flip_0_9_1_out_2), .clk_out(flip_0_9_1_clk_out));
  Hex_Digit_Display hex_digit_display_2 (.value(flip_0_9_1_out_2), .dp(1'b0));
  Flip_0_5 flip_0_5_2 (.clk(flip_0_9_2_clk_out), .out_2(flip_0_5_2_out_2), .clk_out(flip_0_5_2_clk_out));
  Hex_Digit_Display hex_digit_display_3 (.value({1'b0, flip_0_5_2_out_2}), .dp(1'b0));
  Flip_0_9 flip_0_9_2 (.clk(clock_1_out), .out_2(flip_0_9_2_out_2), .clk_out(flip_0_9_2_clk_out));
  Clock clock_1 (.out(clock_1_out));
  Hex_Digit_Display hex_digit_display_4 (.value(flip_0_9_2_out_2), .dp(1'b0));
endmodule
