// Logisim project Ulinha_Desloc_Simples.circ as structural Verilog: 7 circuits, main circuit Célula
module \Célula  (
  input  Right,
  input  A,
  input  B,
  input  Left,
  input  Cin_Bin,
  input  [4:0] Seletor,
  output S,
  output Cout_Bout
);

  wire and_1_out, and_2_out, full_adder_1_cout, full_adder_1_s, full_subtractor_1_bout, full_subtractor_1_s,
       nand_1_out, or_1_out, xor_1_out;

  and and_1 (and_1_out, A, B);
  or or_1 (or_1_out, A, B);
  xor xor_1 (xor_1_out, A, B);
  nand nand_1 (nand_1_out, A, B);
  Full_adder full_adder_1 (.a(A), .b(B), .cin(Cin_Bin), .cout(full_adder_1_cout), .s(full_adder_1_s));
  Full_Subtractor full_subtractor_1 (
    .a(A), .b(B), .bin(Cin_Bin), .bout(full_subtractor_1_bout), .s(full_subtractor_1_s));
  and and_2 (and_2_out, ~Seletor[0], ~Seletor[1], Seletor[2], Seletor[3], ~Seletor[4]);  // AND_Gate
  Multiplexer #(.enable("false")) multiplexer_1 (
    .in0(full_adder_1_cout), .in1(full_subtractor_1_bout), .out(Cout_Bout), .sel(and_2_out));
  Multiplexer #(.select(5), .enable("false")) multiplexer_2 (
    .in0(and_1_out), .in1(or_1_out), .in2(xor_1_out), .in3(nand_1_out), .in4(full_adder_1_s),
    .in5(full_adder_1_s), .in6(full_subtractor_1_s), .in7(Left), .in8(Right), .in9(Right), .out(S),
    .sel(Seletor));  // open: in10, in11, in12, in13, in14, in15, in16, in17, in18, in19, in20, in21, in22, in23, in24, in25, in26, in27, in28, in29, in30, in31

  // Notes on the sheet:
  //   00000 - AND
  //   00001 - OR
  //   00010 - XOR
  //   00011 - NAND
  //   00100 - SOMA_NATURAIS
  //   00101 - SOMA_INTEIROS
  //   00110 - SUBTRAÇÃO
  //   00111 - DESLOCAMENTO ESQUERDA
  //   01000 - DESLOCAMENTO DIREITA
  //   01001- DESLOCAMENTO DIREITA ARI.
endmodule

module Full_adder (
  input  a,
  input  b,
  input  cin,
  output cout,
  output s
);

  wire and_1_out, and_2_out, and_3_out, and_4_out, xor_2_out;

  xor xor_1 (s, cin, xor_2_out);
  xor xor_2 (xor_2_out, a, b);
  and and_1 (and_1_out, ~cin, a, b);  // AND_Gate
  and and_2 (and_2_out, cin, ~a, b);  // AND_Gate
  and and_3 (and_3_out, cin, a, ~b);  // AND_Gate
  and and_4 (and_4_out, cin, a, b);
  or or_1 (cout, and_1_out, and_2_out, and_3_out, and_4_out);
endmodule

module Full_Subtractor (
  input  a,
  input  b,
  input  bin,
  output bout,
  output s
);

  wire and_1_out, and_2_out, and_3_out, and_4_out, and_5_out, and_6_out, and_7_out, not_1_out, not_2_out,
       not_3_out, not_4_out, not_5_out, not_6_out;

  and and_1 (and_1_out, b, bin);
  and and_2 (and_2_out, a, bin);
  and and_3 (and_3_out, a, b);
  not not_1 (not_1_out, a);
  not not_2 (not_2_out, b);
  not not_3 (not_3_out, a);
  not not_4 (not_4_out, bin);
  not not_5 (not_5_out, b);
  not not_6 (not_6_out, bin);
  or or_1 (bout, and_1_out, and_2_out, and_3_out);
  and and_4 (and_4_out, not_1_out, not_2_out, bin);
  and and_5 (and_5_out, not_3_out, b, not_4_out);
  and and_6 (and_6_out, a, not_5_out, not_6_out);
  and and_7 (and_7_out, a, b, bin);
  or or_2 (s, and_4_out, and_5_out, and_6_out, and_7_out);
endmodule

module main (
  input  [31:0] A,
  input  [31:0] B,
  input  [4:0] in_3,
  output [31:0] S,
  output Overflow
);

  wire \célula_1_cout_bout , \célula_2_cout_bout , \célula_3_cout_bout , \célula_4_cout_bout ,
       \célula_5_cout_bout , \célula_6_cout_bout , \célula_7_cout_bout , \célula_8_cout_bout ,
       \célula_9_cout_bout , \célula_10_cout_bout , \célula_11_cout_bout , \célula_12_cout_bout ,
       \célula_13_cout_bout , \célula_14_cout_bout , \célula_15_cout_bout , \célula_16_cout_bout ,
       \célula_17_cout_bout , \célula_18_cout_bout , \célula_19_cout_bout , \célula_20_cout_bout ,
       \célula_21_cout_bout , \célula_22_cout_bout , \célula_23_cout_bout , \célula_24_cout_bout ,
       \célula_25_cout_bout , \célula_26_cout_bout , \célula_27_cout_bout , \célula_28_cout_bout ,
       \célula_29_cout_bout , \célula_30_cout_bout , \célula_31_cout_bout , \célula_msb_1_cout_bout ;

  \Célula  \célula_1  (
    .Left(A[15]), .Cin_Bin(\célula_29_cout_bout ), .A(A[16]), .B(B[16]), .Seletor(in_3), .Right(A[17]),
    .S(S[16]), .Cout_Bout(\célula_1_cout_bout ));
  \Célula  \célula_2  (
    .Left(A[23]), .Cin_Bin(\célula_30_cout_bout ), .A(A[24]), .B(B[24]), .Seletor(in_3), .Right(A[25]),
    .S(S[24]), .Cout_Bout(\célula_2_cout_bout ));
  \Célula  \célula_3  (
    .Left(1'b0), .Cin_Bin(1'b0), .A(A[0]), .B(B[0]), .Seletor(in_3), .Right(A[1]), .S(S[0]),
    .Cout_Bout(\célula_3_cout_bout ));
  \Célula  \célula_4  (
    .Left(A[7]), .Cin_Bin(\célula_31_cout_bout ), .A(A[8]), .B(B[8]), .Seletor(in_3), .Right(A[9]), .S(S[8]),
    .Cout_Bout(\célula_4_cout_bout ));
  \Célula  \célula_5  (
    .Left(A[16]), .Cin_Bin(\célula_1_cout_bout ), .A(A[17]), .B(B[17]), .Seletor(in_3), .Right(A[18]),
    .S(S[17]), .Cout_Bout(\célula_5_cout_bout ));
  \Célula  \célula_6  (
    .Left(A[24]), .Cin_Bin(\célula_2_cout_bout ), .A(A[25]), .B(B[25]), .Seletor(in_3), .Right(A[26]),
    .S(S[25]), .Cout_Bout(\célula_6_cout_bout ));
  \Célula  \célula_7  (
    .Left(A[0]), .Cin_Bin(\célula_3_cout_bout ), .A(A[1]), .B(B[1]), .Seletor(in_3), .Right(A[2]), .S(S[1]),
    .Cout_Bout(\célula_7_cout_bout ));
  \Célula  \célula_8  (
    .Left(A[8]), .Cin_Bin(\célula_4_cout_bout ), .A(A[9]), .B(B[9]), .Seletor(in_3), .Right(A[10]), .S(S[9]),
    .Cout_Bout(\célula_8_cout_bout ));
  \Célula  \célula_9  (
    .Left(A[1]), .Cin_Bin(\célula_7_cout_bout ), .A(A[2]), .B(B[2]), .Seletor(in_3), .Right(A[3]), .S(S[2]),
    .Cout_Bout(\célula_9_cout_bout ));
  \Célula  \célula_10  (
    .Left(A[9]), .Cin_Bin(\célula_8_cout_bout ), .A(A[10]), .B(B[10]), .Seletor(in_3), .Right(A[11]),
    .S(S[10]), .Cout_Bout(\célula_10_cout_bout ));
  \Célula  \célula_11  (
    .Left(A[17]), .Cin_Bin(\célula_5_cout_bout ), .A(A[18]), .B(B[18]), .Seletor(in_3), .Right(A[19]),
    .S(S[18]), .Cout_Bout(\célula_11_cout_bout ));
  \Célula  \célula_12  (
    .Left(A[25]), .Cin_Bin(\célula_6_cout_bout ), .A(A[26]), .B(B[26]), .Seletor(in_3), .Right(A[27]),
    .S(S[26]), .Cout_Bout(\célula_12_cout_bout ));
  \Célula  \célula_13  (
    .Left(A[2]), .Cin_Bin(\célula_9_cout_bout ), .A(A[3]), .B(B[3]), .Seletor(in_3), .Right(A[4]), .S(S[3]),
    .Cout_Bout(\célula_13_cout_bout ));
  \Célula  \célula_14  (
    .Left(A[10]), .Cin_Bin(\célula_10_cout_bout ), .A(A[11]), .B(B[11]), .Seletor(in_3), .Right(A[12]),
    .S(S[11]), .Cout_Bout(\célula_14_cout_bout ));
  \Célula  \célula_15  (
    .Left(A[18]), .Cin_Bin(\célula_11_cout_bout ), .A(A[19]), .B(B[19]), .Seletor(in_3), .Right(A[20]),
    .S(S[19]), .Cout_Bout(\célula_15_cout_bout ));
  \Célula  \célula_16  (
    .Left(A[26]), .Cin_Bin(\célula_12_cout_bout ), .A(A[27]), .B(B[27]), .Seletor(in_3), .Right(A[28]),
    .S(S[27]), .Cout_Bout(\célula_16_cout_bout ));
  \Célula  \célula_17  (
    .Left(A[3]), .Cin_Bin(\célula_13_cout_bout ), .A(A[4]), .B(B[4]), .Seletor(in_3), .Right(A[5]), .S(S[4]),
    .Cout_Bout(\célula_17_cout_bout ));
  \Célula  \célula_18  (
    .Left(A[11]), .Cin_Bin(\célula_14_cout_bout ), .A(A[12]), .B(B[12]), .Seletor(in_3), .Right(A[13]),
    .S(S[12]), .Cout_Bout(\célula_18_cout_bout ));
  \Célula  \célula_19  (
    .Left(A[19]), .Cin_Bin(\célula_15_cout_bout ), .A(A[20]), .B(B[20]), .Seletor(in_3), .Right(A[21]),
    .S(S[20]), .Cout_Bout(\célula_19_cout_bout ));
  \Célula  \célula_20  (
    .Left(A[27]), .Cin_Bin(\célula_16_cout_bout ), .A(A[28]), .B(B[28]), .Seletor(in_3), .Right(A[29]),
    .S(S[28]), .Cout_Bout(\célula_20_cout_bout ));
  \Célula  \célula_21  (
    .Left(A[4]), .Cin_Bin(\célula_17_cout_bout ), .A(A[5]), .B(B[5]), .Seletor(in_3), .Right(A[6]), .S(S[5]),
    .Cout_Bout(\célula_21_cout_bout ));
  \Célula  \célula_22  (
    .Left(A[12]), .Cin_Bin(\célula_18_cout_bout ), .A(A[13]), .B(B[13]), .Seletor(in_3), .Right(A[14]),
    .S(S[13]), .Cout_Bout(\célula_22_cout_bout ));
  \Célula  \célula_23  (
    .Left(A[20]), .Cin_Bin(\célula_19_cout_bout ), .A(A[21]), .B(B[21]), .Seletor(in_3), .Right(A[22]),
    .S(S[21]), .Cout_Bout(\célula_23_cout_bout ));
  \Célula  \célula_24  (
    .Left(A[28]), .Cin_Bin(\célula_20_cout_bout ), .A(A[29]), .B(B[29]), .Seletor(in_3), .Right(A[30]),
    .S(S[29]), .Cout_Bout(\célula_24_cout_bout ));
  \Célula  \célula_25  (
    .Left(A[21]), .Cin_Bin(\célula_23_cout_bout ), .A(A[22]), .B(B[22]), .Seletor(in_3), .Right(A[23]),
    .S(S[22]), .Cout_Bout(\célula_25_cout_bout ));
  \Célula  \célula_26  (
    .Left(A[29]), .Cin_Bin(\célula_24_cout_bout ), .A(A[30]), .B(B[30]), .Seletor(in_3), .Right(A[31]),
    .S(S[30]), .Cout_Bout(\célula_26_cout_bout ));
  \Célula  \célula_27  (
    .Left(A[5]), .Cin_Bin(\célula_21_cout_bout ), .A(A[6]), .B(B[6]), .Seletor(in_3), .Right(A[7]), .S(S[6]),
    .Cout_Bout(\célula_27_cout_bout ));
  \Célula  \célula_28  (
    .Left(A[13]), .Cin_Bin(\célula_22_cout_bout ), .A(A[14]), .B(B[14]), .Seletor(in_3), .Right(A[15]),
    .S(S[14]), .Cout_Bout(\célula_28_cout_bout ));
  \Célula  \célula_29  (
    .Left(A[14]), .Cin_Bin(\célula_28_cout_bout ), .A(A[15]), .B(B[15]), .Seletor(in_3), .Right(A[16]),
    .S(S[15]), .Cout_Bout(\célula_29_cout_bout ));
  \Célula  \célula_30  (
    .Left(A[22]), .Cin_Bin(\célula_25_cout_bout ), .A(A[23]), .B(B[23]), .Seletor(in_3), .Right(A[24]),
    .S(S[23]), .Cout_Bout(\célula_30_cout_bout ));
  \Célula_MSB  \célula_msb_1  (
    .Left(A[30]), .Cin_Bin(\célula_26_cout_bout ), .A(A[31]), .B(B[31]), .Right_Ar(A[31]), .Seletor(in_3),
    .Right(1'b0), .S(S[31]), .Cout_Bout(\célula_msb_1_cout_bout ));
  \Célula  \célula_31  (
    .Left(A[6]), .Cin_Bin(\célula_27_cout_bout ), .A(A[7]), .B(B[7]), .Seletor(in_3), .Right(A[8]), .S(S[7]),
    .Cout_Bout(\célula_31_cout_bout ));
  Overflow_Controller overflow_controller_1 (
    .CoutMSB(\célula_msb_1_cout_bout ), .s(S[31]), .a(A[31]), .b(B[31]), .OpCode(in_3), .Overflow(Overflow));

  // Notes on the sheet:
  //   00000 - AND
  //   00001 - OR
  //   00010 - XOR
  //   00011 - NAND
  //   00100 - SOMA_NATURAIS
  //   00101 - SOMA_INTEIROS
  //   00110 - SUBTRAÇÃO
  //   01000 - DESLOCAMENTO DIREITA
  //   00111 - DESLOCAMENTO ESQUERDA
  //   01001- DESLOCAMENTO DIREITA ARI.
endmodule

module Overflow_Controller (
  input  CoutMSB,
  input  a,
  input  b,
  input  s,
  input  [4:0] OpCode,
  output Overflow
);

  wire and_1_out, and_2_out, and_3_out, or_1_out;

  Multiplexer #(.enable("false")) multiplexer_1 (.in0(CoutMSB), .in1(or_1_out), .out(Overflow), .sel(and_1_out));
  or or_1 (or_1_out, and_2_out, and_3_out);
  and and_1 (and_1_out, ~OpCode[0], ~OpCode[1], OpCode[2], OpCode[3], ~OpCode[4]);  // AND_Gate
  and and_2 (and_2_out, a, b, ~s);  // AND_Gate
  and and_3 (and_3_out, ~a, ~b, s);  // AND_Gate
endmodule

module \Célula_MSB  (
  input  Right,
  input  A,
  input  B,
  input  Left,
  input  Right_Ar,
  input  Cin_Bin,
  input  [4:0] Seletor,
  output S,
  output Cout_Bout
);

  wire and_1_out, and_2_out, full_adder_1_cout, full_adder_1_s, full_subtractor_1_bout, full_subtractor_1_s,
       nand_1_out, or_1_out, xor_1_out;

  and and_1 (and_1_out, A, B);
  or or_1 (or_1_out, A, B);
  xor xor_1 (xor_1_out, A, B);
  nand nand_1 (nand_1_out, A, B);
  Full_adder full_adder_1 (.a(A), .b(B), .cin(Cin_Bin), .cout(full_adder_1_cout), .s(full_adder_1_s));
  Full_Subtractor full_subtractor_1 (
    .a(A), .b(B), .bin(Cin_Bin), .bout(full_subtractor_1_bout), .s(full_subtractor_1_s));
  and and_2 (and_2_out, ~Seletor[0], ~Seletor[1], Seletor[2], Seletor[3], ~Seletor[4]);  // AND_Gate
  Multiplexer #(.enable("false")) multiplexer_1 (
    .in0(full_adder_1_cout), .in1(full_subtractor_1_bout), .out(Cout_Bout), .sel(and_2_out));
  Multiplexer #(.select(5), .enable("false")) multiplexer_2 (
    .in0(and_1_out), .in1(or_1_out), .in2(xor_1_out), .in3(nand_1_out), .in4(full_adder_1_s),
    .in5(full_adder_1_s), .in6(full_subtractor_1_s), .in7(Left), .in8(Right), .in9(Right_Ar), .out(S),
    .sel(Seletor));  // open: in10, in11, in12, in13, in14, in15, in16, in17, in18, in19, in20, in21, in22, in23, in24, in25, in26, in27, in28, in29, in30, in31
endmodule

module Teste_bagaceira (
  input  [4:0] in_1,
  input  [4:0] in_2,
  input  [2:0] in_3
);

  Shifter #(.width(5), .shift("ar")) shifter_1 (.in(in_1), .\dist (in_3), .out(in_2));
endmodule
